# Fritzing sketch logger (saved by Fritzing 0.7.4b)
breadboards: 1

parts:
  U2 = Arduino Mega
  J1 = screw terminal, 6 pins
  U3 = Voltage Regulator - 3.3V [package="TO220 [THT]"]
  C1 = Electrolytic Capacitor [capacitance=1µF package="100 mil [THT, electrolytic]"]
  C2 = Electrolytic Capacitor [capacitance=1µF package="100 mil [THT, electrolytic]"]
  C3 = Electrolytic Capacitor [capacitance=1µF package="100 mil [THT, electrolytic]"]
  C4 = Electrolytic Capacitor [capacitance=1µF package="100 mil [THT, electrolytic]"]
  74AHC1 = SN74AHC125
  R2 = Resistor [tolerance=±5% resistance=10k package=THT]
  MMA1 = MMA8452
  GPSBRD1 = Adafruit ultimate GPS Breakout board
  Q1 = NPN-Transistor [package="TO92 [THT]"]
  LED1 = LED - 3mm [color="Red (633nm)" package="3 mm [THT]"]
  R3 = Resistor [tolerance=±5% resistance=220 package=THT]
  IOP = SO08 [chip_label=IC spacing=300mil package=SO]
  RG = Resistor [tolerance=±5% resistance=220 package=THT]
  Q2 = NPN-Transistor [package="TO92 [THT]"]
  R5 = Resistor [tolerance=±5% resistance=220 package=THT]
  R6 = Resistor [tolerance=±5% resistance=220 package=THT]
  GTPA1 = gtop gps p6c
  D1 = Rectifier Diode [part_number=1N4001 package="Melf DO-213 AB [SMD]"]
  R7 = Resistor [tolerance=±5% resistance=10k package="1206 [SMD]"]
  R8 = Resistor [tolerance=±5% resistance=220 package=THT]
  R9 = Resistor [tolerance=±5% resistance=220 package=THT]
  L1 = rectifier
  R10 = Resistor [tolerance=±5% resistance=220 package=THT]
  SDC2 = SD Card Connector
  1220 = Coin_Battery_1220

nets:
  GND: U2.GND, J1.pin1, U3.GND, C1.-, C2.-, C3.-, C4.-, 74AHC1.1OE, 74AHC1.2OE, 74AHC1.GND, 74AHC1.4OE, 74AHC1.3OE, MMA1.GND, GPSBRD1.GND, R3.Pin_1, IOP.5, IOP.6, R5.Pin_0, R6.Pin_0, GTPA1.GND, R8.Pin_1, R9.Pin_0, R10.Pin_1, SDC2.VSS, SDC2.VSS2, SDC2.GND, SDC2.no_name_yet, 1220.V-
  N1: U2.D4, LED1.anode
  N2: U2.D3, MMA1.I1
  N3: U2.D2, MMA1.I2
  +5V: U2.+5V, U3.input_voltage, C1.+, C2.+, R2.Pin_1, GPSBRD1.VIN, Q1.E, IOP.8, Q2.E
  N4: U2.A0, IOP.7
  N5: U2.D14, GPSBRD1.RX, D1.cathode
  N6: U2.D15, GPSBRD1.TX, GTPA1.TX
  N7: U2.D18, Q1.C, R9.Pin_1
  N8: U2.D19, Q2.C, R8.Pin_0
  N9: U2.D20, MMA1.SDA
  N10: U2.D21, MMA1.SCL
  N11: U2.D50, SDC2.DO
  N12: U2.D51, 74AHC1.1A
  N13: U2.D52, 74AHC1.3A
  N14: U2.D53, 74AHC1.2A, R2.Pin_0
  N15: J1.pin3, Q2.B, R5.Pin_1
  N16: J1.pin4, Q1.B, R6.Pin_1
  N17: J1.pin5, IOP.4
  N18: J1.pin6, IOP.1, R10.Pin_0
  VCC: U3.output_voltage, C3.+, C4.+, 74AHC1.VCC, MMA1.3.3V, R7.Pin_1, L1.no_name_yet#0, SDC2.VDD
  N19: 74AHC1.1Y, SDC2.DI
  N20: 74AHC1.2Y, SDC2.CS
  N21: 74AHC1.3Y, SDC2.SCLK
  N22: GPSBRD1.VBAT, GTPA1.VBAT, 1220.V+
  N23: LED1.cathode, R3.Pin_0
  N24: IOP.2, RG.Pin_0
  N25: IOP.3, RG.Pin_1
  N26: GTPA1.VCC, L1.no_name_yet#1
  N27: GTPA1.RX, D1.anode, R7.Pin_0

notes:
  -D +D IG- SP    GND
  slipangle.us

custom parts:
  SN74AHC125: Quad Buffer/Line Driver, 3 State. Inputs Outputs xOE xA xY L L L L H H H X Z Where L = low, H = high, X = don't care, Z = high impedence OFF state
  SD Card Connector: SD Card Connector, push-pull type. For example schematic see: http://www.ladyada.net/images/logshield/logschemv1.png
